// Logisim project Masomenos.circ as structural Verilog: 4 circuits, main circuit main
module main (
  input  PA,
  input  PB,
  input  E,
  input  TB,
  input  PA_2
);

  wire clock_1_out, d_ff_1_q, d_ff_2_q, deco_1_amarillo, deco_1_rojo, deco_1_verde, deco_2_amarillo,
       deco_2_rojo, deco_2_verde, final_1_s00, final_1_s11, not_1_out, not_2_out, salidas_1_la0,
       salidas_1_la1, salidas_1_lb0, salidas_1_lb1, salidas_1_pa, salidas_1_pb;

  Final final_1 (
    .S1(d_ff_1_q), .S0(d_ff_2_q), .PA(PA), .PB(PB), .E(E), .TB(TB), .TA(PA_2), .S11(final_1_s11),
    .S00(final_1_s00));
  Clock clock_1 (.out(clock_1_out));
  D_Flip_Flop d_ff_1 (.clk(clock_1_out), .D(final_1_s11), .Q(d_ff_1_q));  // open: Qn, preset, en, reset
  D_Flip_Flop d_ff_2 (.clk(clock_1_out), .D(final_1_s00), .Q(d_ff_2_q));  // open: Qn, preset, en, reset
  Salidas salidas_1 (
    .S1(d_ff_1_q), .S0(d_ff_2_q), .LA1(salidas_1_la1), .LA0(salidas_1_la0), .LB1(salidas_1_lb1),
    .LB0(salidas_1_lb0), .PA(salidas_1_pa), .PB(salidas_1_pb));
  DECO deco_1 (
    .L1(salidas_1_la1), .L0(salidas_1_la0), .VERDE(deco_1_verde), .AMARILLO(deco_1_amarillo),
    .ROJO(deco_1_rojo));
  DECO deco_2 (
    .L1(salidas_1_lb1), .L0(salidas_1_lb0), .VERDE(deco_2_verde), .AMARILLO(deco_2_amarillo),
    .ROJO(deco_2_rojo));
  not not_1 (not_1_out, salidas_1_pa);
  not not_2 (not_2_out, salidas_1_pb);
  LED led_1 (.in(deco_1_verde));
  LED led_2 (.in(deco_1_amarillo));
  LED led_3 (.in(deco_1_rojo));
  LED led_4 (.in(deco_2_verde));
  LED led_5 (.in(deco_2_amarillo));
  LED led_6 (.in(deco_2_rojo));
  LED led_7 (.in(not_1_out));
  LED led_8 (.in(salidas_1_pa));
  LED led_9 (.in(not_2_out));
  LED led_10 (.in(salidas_1_pb));
endmodule

module Final (
  input  S1,
  input  S0,
  input  PA,
  input  PB,
  input  E,
  input  TB,
  input  TA,
  output S11,
  output S00
);

  wire and_1_out, and_2_out, and_3_out, and_4_out, and_5_out, and_6_out, and_7_out, and_8_out, and_9_out,
       and_10_out, and_11_out, and_12_out, and_13_out, and_14_out, not_1_out, not_2_out, not_3_out,
       not_4_out, not_5_out, not_6_out, not_7_out, not_8_out, not_9_out, not_10_out, not_11_out, not_12_out,
       not_13_out, not_14_out, not_15_out, not_16_out, not_17_out, not_18_out, not_19_out, not_20_out,
       not_21_out, not_22_out, not_23_out, not_24_out, not_25_out, not_26_out, not_27_out, not_28_out,
       not_29_out, not_30_out, not_31_out, not_32_out, not_33_out, not_34_out, not_35_out, not_36_out,
       not_37_out, not_38_out, not_39_out, not_40_out, not_41_out, not_42_out;

  not not_1 (not_1_out, S1);
  not not_2 (not_2_out, PA);
  not not_3 (not_3_out, E);
  not not_4 (not_4_out, S1);
  not not_5 (not_5_out, PB);
  not not_6 (not_6_out, E);
  not not_7 (not_7_out, S1);
  not not_8 (not_8_out, E);
  not not_9 (not_9_out, S1);
  not not_10 (not_10_out, E);
  not not_11 (not_11_out, S1);
  not not_12 (not_12_out, TB);
  not not_13 (not_13_out, TA);
  not not_14 (not_14_out, S0);
  not not_15 (not_15_out, PA);
  not not_16 (not_16_out, PB);
  not not_17 (not_17_out, E);
  not not_18 (not_18_out, S0);
  not not_19 (not_19_out, E);
  not not_20 (not_20_out, S0);
  not not_21 (not_21_out, E);
  not not_22 (not_22_out, S0);
  not not_23 (not_23_out, TB);
  not not_24 (not_24_out, TA);
  not not_25 (not_25_out, S0);
  not not_26 (not_26_out, PA);
  not not_27 (not_27_out, PB);
  not not_28 (not_28_out, E);
  not not_29 (not_29_out, TB);
  not not_30 (not_30_out, TA);
  not not_31 (not_31_out, S1);
  not not_32 (not_32_out, S0);
  not not_33 (not_33_out, S0);
  not not_34 (not_34_out, PA);
  not not_35 (not_35_out, PB);
  not not_36 (not_36_out, E);
  not not_37 (not_37_out, TB);
  not not_38 (not_38_out, S0);
  not not_39 (not_39_out, E);
  not not_40 (not_40_out, S0);
  not not_41 (not_41_out, TB);
  not not_42 (not_42_out, TA);
  and and_1 (and_1_out, not_1_out, S0, not_2_out, not_3_out);
  and and_2 (and_2_out, not_4_out, S0, not_5_out, not_6_out);
  and and_3 (and_3_out, not_7_out, S0, not_8_out, TA);
  and and_4 (and_4_out, not_9_out, S0, not_10_out, TB);
  and and_5 (and_5_out, not_11_out, S0, PA, PB, E, not_12_out, not_13_out);
  and and_6 (and_6_out, S1, not_14_out, not_15_out, not_16_out, not_17_out);
  and and_7 (and_7_out, S1, not_18_out, not_19_out, TA);
  and and_8 (and_8_out, S1, not_20_out, not_21_out, TB);
  and and_9 (and_9_out, S1, not_22_out, E, not_23_out, not_24_out);
  and and_10 (and_10_out, not_25_out, not_26_out, not_27_out, not_28_out, not_29_out, not_30_out);
  and and_11 (and_11_out, not_31_out, not_32_out, PA, TA);
  and and_12 (and_12_out, S1, not_33_out, not_34_out, not_35_out, not_36_out, not_37_out);
  and and_13 (and_13_out, S1, not_38_out, PB, not_39_out, TB, TA);
  and and_14 (and_14_out, S1, not_40_out, PB, E, not_41_out, not_42_out);
  or or_1 (S00, and_10_out, and_11_out, and_12_out, and_13_out, and_14_out);
  or or_2 (S11, and_1_out, and_2_out, and_3_out, and_4_out, and_5_out, and_6_out, and_7_out, and_8_out, and_9_out);
endmodule

module Salidas (
  input  S1,
  input  S0,
  output LA1,
  output LA0,
  output LB1,
  output LB0,
  output PA,
  output PB
);

  wire not_1_out, not_3_out, not_4_out, not_5_out;

  not not_1 (not_1_out, S1);
  not not_2 (LB1, S1);
  and and_1 (LB0, S1, S0);
  not not_3 (not_3_out, S0);
  not not_4 (not_4_out, S1);
  not not_5 (not_5_out, S0);
  and and_2 (LA0, not_1_out, S0);
  and and_3 (PA, S1, not_3_out);
  and and_4 (PB, not_4_out, not_5_out);

  assign LA1 = S1;
endmodule

module DECO (
  input  L1,
  input  L0,
  output VERDE,
  output AMARILLO,
  output ROJO
);

  wire not_1_out, not_2_out, not_3_out, not_4_out;

  not not_1 (not_1_out, L1);
  not not_2 (not_2_out, L0);
  not not_3 (not_3_out, L1);
  not not_4 (not_4_out, L0);
  and and_1 (VERDE, not_1_out, not_2_out);
  and and_2 (AMARILLO, not_3_out, L0);
  and and_3 (ROJO, L1, not_4_out);
endmodule
