// Logisim project Ripple carry.circ as structural Verilog: 4 circuits, main circuit Full adder
module Full_adder (
  input  Ci,
  input  A,
  input  B,
  output S,
  output Co
);

  wire and_1_out, and_2_out, xor_1_out;

  and and_1 (and_1_out, A, B);
  xor xor_1 (xor_1_out, B, A);
  and and_2 (and_2_out, Ci, xor_1_out);
  xor xor_2 (S, Ci, xor_1_out);
  or or_1 (Co, and_2_out, and_1_out);
endmodule

module X2 (
  input  Ci,
  input  A0,
  input  B0,
  input  A1,
  input  B1,
  output S0,
  output S1,
  output CO
);

  wire full_adder_1_co;

  Full_adder full_adder_1 (.Ci(Ci), .A(A0), .B(B0), .S(S0), .Co(full_adder_1_co));
  Full_adder full_adder_2 (.Ci(full_adder_1_co), .A(A1), .B(B1), .S(S1), .Co(CO));
endmodule

module X4 (
  input  Ci,
  input  A0,
  input  B0,
  input  A1,
  input  B1,
  input  A2,
  input  B2,
  input  A3,
  input  B3,
  output S0,
  output S1,
  output S2,
  output S3,
  output CO
);

  wire x2_1_co;

  X2 x2_1 (.Ci(Ci), .A0(A0), .B0(B0), .A1(A1), .B1(B1), .S0(S0), .S1(S1), .CO(x2_1_co));
  X2 x2_2 (.Ci(x2_1_co), .A0(A2), .B0(B2), .A1(A3), .B1(B3), .S0(S2), .S1(S3), .CO(CO));
endmodule

module X8 (
  input  Ci,
  input  A0,
  input  B0,
  input  A1,
  input  B1,
  input  A2,
  input  B2,
  input  A3,
  input  B3,
  input  A4,
  input  B4,
  input  A5,
  input  B5,
  input  A6,
  input  B6,
  input  A7,
  input  B7,
  output S0,
  output S1,
  output S2,
  output S3,
  output S4,
  output S5,
  output S6,
  output S7,
  output CO
);

  wire x4_1_co;

  X4 x4_1 (
    .Ci(Ci), .A0(A0), .B0(B0), .A1(A1), .B1(B1), .A2(A2), .B2(B2), .A3(A3), .B3(B3), .S0(S0), .S1(S1),
    .S2(S2), .S3(S3), .CO(x4_1_co));
  X4 x4_2 (
    .Ci(x4_1_co), .A0(A4), .B0(B4), .A1(A5), .B1(B5), .A2(A6), .B2(B6), .A3(A7), .B3(B7), .S0(S4), .S1(S5),
    .S2(S6), .S3(S7), .CO(CO));
endmodule
