// Logisim project prefix stone.circ as structural Verilog: 5 circuits, main circuit main
module main (
);

  wire amarillo_1_g, amarillo_1_p, amarillo_2_g, amarillo_2_p, amarillo_3_g, amarillo_3_p, amarillo_5_g,
       rojo_1_g, rojo_1_p, rojo_2_g, rojo_2_p, rojo_3_g, rojo_4_g, rojo_4_p, suma_1_si, suma_2_si, suma_3_si,
       suma_4_si, verde_1_g, verde_1_p;

  Rojo rojo_1 (.Ai(1'b0), .Bi(1'b0), .P(rojo_1_p), .G(rojo_1_g));
  Rojo rojo_2 (.Ai(1'b1), .Bi(1'b1), .P(rojo_2_p), .G(rojo_2_g));
  Rojo rojo_3 (.Ai(1'b0), .Bi(1'b0), .P(rojo_1_p), .G(rojo_3_g));
  Rojo rojo_4 (.Ai(1'b0), .Bi(1'b1), .P(rojo_4_p), .G(rojo_4_g));
  Suma suma_1 (.Pi(rojo_1_p), .Ci_1(1'b0), .Si(suma_1_si));
  Suma suma_2 (.Pi(rojo_2_p), .Ci_1(rojo_1_g), .Si(suma_2_si));
  Suma suma_3 (.Pi(rojo_1_p), .Ci_1(rojo_2_g), .Si(suma_3_si));
  Suma suma_4 (.Pi(rojo_4_p), .Ci_1(rojo_3_g), .Si(suma_4_si));
  Verde verde_1 (.Pi(rojo_1_p), .Gi(rojo_1_g), .P(verde_1_p), .G(verde_1_g));
  Amarillo amarillo_1 (
    .Pi_1(rojo_1_g), .Pi(rojo_2_p), .Gi_1(rojo_1_p), .Gi(rojo_2_g), .P(amarillo_1_p), .G(amarillo_1_g));
  Amarillo amarillo_2 (
    .Pi_1(rojo_2_p), .Pi(rojo_1_p), .Gi_1(rojo_2_g), .Gi(rojo_3_g), .P(amarillo_2_p), .G(amarillo_2_g));
  Amarillo amarillo_3 (
    .Pi_1(rojo_1_p), .Pi(rojo_4_p), .Gi_1(rojo_3_g), .Gi(rojo_4_g), .P(amarillo_3_p), .G(amarillo_3_g));
  LED led_1 (.in(suma_4_si));
  LED led_2 (.in(amarillo_5_g));
  LED led_3 (.in(suma_3_si));
  Verde verde_2 (.Pi(verde_1_p), .Gi(verde_1_g));  // open: P, G
  Verde verde_3 (.Pi(amarillo_1_p), .Gi(amarillo_1_g));  // open: P, G
  Amarillo amarillo_4 (.Pi_1(verde_1_p), .Pi(amarillo_2_p), .Gi_1(verde_1_g), .Gi(amarillo_2_g));  // open: P, G
  Amarillo amarillo_5 (
    .Pi_1(amarillo_1_p), .Pi(amarillo_3_p), .Gi_1(amarillo_1_g), .Gi(amarillo_3_g), .G(amarillo_5_g));  // open: P
  LED led_4 (.in(suma_2_si));
  LED led_5 (.in(suma_1_si));

  // Notes on the sheet:
  //   Carry in
  //   A0
  //   B0
  //   A1
  //   B1
  //   A2
  //   B2
  //   A3
  //   B3
  //   S3
  //   Cout
  //   S2
  //   S1
  //   S0
endmodule

module Rojo (
  input  Ai,
  input  Bi,
  output P,
  output G
);

  and and_1 (G, Ai, Bi);
  xor xor_1 (P, Ai, Bi);
endmodule

module Amarillo (
  input  Pi_1,
  input  Pi,
  input  Gi_1,
  input  Gi,
  output P,
  output G
);

  wire and_2_out;

  and and_1 (P, Pi_1, Pi);
  and and_2 (and_2_out, Pi, Gi_1);
  or or_1 (G, and_2_out, Gi);
endmodule

module Verde (
  input  Pi,
  input  Gi,
  output P,
  output G
);


  assign G = Gi;
  assign P = Pi;
endmodule

module Suma (
  input  Pi,
  input  Ci_1,
  output Si
);

  xor xor_1 (Si, Pi, Ci_1);
endmodule
